// Logisim project hw5evolution.circ as structural Verilog: 13 circuits, main circuit MyXOR
module MyXOR (
  input  in_1,
  input  in_2,
  output out_3
);

  wire and_1_out, and_2_out, not_1_out, not_2_out;

  not not_1 (not_1_out, in_2);
  not not_2 (not_2_out, in_1);
  and and_1 (and_1_out, not_1_out, in_1);
  and and_2 (and_2_out, not_2_out, in_2);
  or or_1 (out_3, and_1_out, and_2_out);

  // Notes on the sheet:
  //   Here is a location to build an XOR circuit
  //   You can follow the tutorial (Help menu - "tutorial") or work on your own...
endmodule

module FullAdder (
  input  X,
  input  Y,
  input  CarryIn,
  output Sum,
  output CarryOut
);

  wire and_1_out, and_2_out, and_3_out, and_4_out, and_5_out, and_6_out, and_7_out, and_8_out, not_1_out,
       not_2_out, not_3_out;

  not not_1 (not_1_out, X);
  not not_2 (not_2_out, Y);
  not not_3 (not_3_out, CarryIn);
  and and_1 (and_1_out, X, Y, CarryIn);
  and and_2 (and_2_out, not_1_out, not_2_out, CarryIn);
  and and_3 (and_3_out, X, not_2_out, not_3_out);
  and and_4 (and_4_out, not_1_out, Y, not_3_out);
  and and_5 (and_5_out, not_1_out, Y, CarryIn);
  and and_6 (and_6_out, X, Y, CarryIn);
  and and_7 (and_7_out, X, not_2_out, CarryIn);
  and and_8 (and_8_out, X, Y, not_3_out);
  or or_1 (Sum, and_1_out, and_2_out, and_3_out, and_4_out);
  or or_2 (CarryOut, and_5_out, and_6_out, and_7_out, and_8_out);

  // Notes on the sheet:
  //   3 input bits:  X,  Y,  and CarryIn
  //   Here is a location to build an FULL ADDER circuit
  //   (1) draw the other four rails   (2) you'll need 8 AND gates    (3)  you'll need 2 OR gates
  //   two output bits:  Sum and CarryOut
endmodule

module A_4bit_Ripple_Carry_Adder (
  input  Y3,
  input  Y2,
  input  Y1,
  input  Y0,
  input  X3,
  input  X2,
  input  X1,
  input  X0,
  output Sum4,
  output Sum3,
  output Sum2,
  output Sum1,
  output Sum0
);

  wire fulladder_2_carryout, fulladder_3_carryout, fulladder_4_carryout;

  FullAdder fulladder_1 (.X(Y3), .Y(X3), .CarryIn(fulladder_2_carryout), .Sum(Sum3), .CarryOut(Sum4));
  FullAdder fulladder_2 (.X(Y2), .Y(X2), .CarryIn(fulladder_3_carryout), .Sum(Sum2), .CarryOut(fulladder_2_carryout));
  FullAdder fulladder_3 (.X(Y1), .Y(X1), .CarryIn(fulladder_4_carryout), .Sum(Sum1), .CarryOut(fulladder_3_carryout));
  FullAdder fulladder_4 (.X(Y0), .Y(X0), .CarryIn(1'b0), .Sum(Sum0), .CarryOut(fulladder_4_carryout));

  // Notes on the sheet:
  //   Here is a location to build an 4-bit RIPPLE-CARRY ADDER circuit
  //   8 input bits
  //   5 output bits
endmodule

module A_4bit_Multiplier (
  input  Y3,
  input  Y2,
  input  Y1,
  input  Y0,
  input  X3,
  input  X2,
  input  X1,
  input  X0,
  output Z7,
  output Z6,
  output Z5,
  output Z4,
  output Z3,
  output Z2,
  output Z1,
  output Z0
);

  wire a_4bit_ripple_carry_adder_2_sum1, a_4bit_ripple_carry_adder_2_sum2, a_4bit_ripple_carry_adder_2_sum3,
       a_4bit_ripple_carry_adder_2_sum4, a_4bit_ripple_carry_adder_3_sum1, a_4bit_ripple_carry_adder_3_sum2,
       a_4bit_ripple_carry_adder_3_sum3, a_4bit_ripple_carry_adder_3_sum4, a_4x1_multiplier_1_out_6,
       a_4x1_multiplier_1_out_7, a_4x1_multiplier_1_out_8, a_4x1_multiplier_1_out_9,
       a_4x1_multiplier_2_out_6, a_4x1_multiplier_2_out_7, a_4x1_multiplier_2_out_8,
       a_4x1_multiplier_2_out_9, a_4x1_multiplier_3_out_6, a_4x1_multiplier_3_out_7,
       a_4x1_multiplier_3_out_8, a_4x1_multiplier_3_out_9, a_4x1_multiplier_4_out_7,
       a_4x1_multiplier_4_out_8, a_4x1_multiplier_4_out_9;

  A_4x1_Multiplier a_4x1_multiplier_1 (
    .Y3(Y3), .Y2(Y2), .Y1(Y1), .Y0(Y0), .X(X3), .out_6(a_4x1_multiplier_1_out_6),
    .out_7(a_4x1_multiplier_1_out_7), .out_8(a_4x1_multiplier_1_out_8), .out_9(a_4x1_multiplier_1_out_9));
  A_4x1_Multiplier a_4x1_multiplier_2 (
    .Y3(Y3), .Y2(Y2), .Y1(Y1), .Y0(Y0), .X(X2), .out_6(a_4x1_multiplier_2_out_6),
    .out_7(a_4x1_multiplier_2_out_7), .out_8(a_4x1_multiplier_2_out_8), .out_9(a_4x1_multiplier_2_out_9));
  A_4bit_Ripple_Carry_Adder a_4bit_ripple_carry_adder_1 (
    .Y3(a_4bit_ripple_carry_adder_2_sum4), .X3(a_4x1_multiplier_1_out_9),
    .Y2(a_4bit_ripple_carry_adder_2_sum3), .X2(a_4x1_multiplier_1_out_8),
    .Y1(a_4bit_ripple_carry_adder_2_sum2), .X1(a_4x1_multiplier_1_out_7),
    .Y0(a_4bit_ripple_carry_adder_2_sum1), .X0(a_4x1_multiplier_1_out_6), .Sum4(Z7), .Sum3(Z6), .Sum2(Z5),
    .Sum1(Z4), .Sum0(Z3));
  A_4x1_Multiplier a_4x1_multiplier_3 (
    .Y3(Y3), .Y2(Y2), .Y1(Y1), .Y0(Y0), .X(X1), .out_6(a_4x1_multiplier_3_out_6),
    .out_7(a_4x1_multiplier_3_out_7), .out_8(a_4x1_multiplier_3_out_8), .out_9(a_4x1_multiplier_3_out_9));
  A_4bit_Ripple_Carry_Adder a_4bit_ripple_carry_adder_2 (
    .Y3(a_4bit_ripple_carry_adder_3_sum4), .X3(a_4x1_multiplier_2_out_9),
    .Y2(a_4bit_ripple_carry_adder_3_sum3), .X2(a_4x1_multiplier_2_out_8),
    .Y1(a_4bit_ripple_carry_adder_3_sum2), .X1(a_4x1_multiplier_2_out_7),
    .Y0(a_4bit_ripple_carry_adder_3_sum1), .X0(a_4x1_multiplier_2_out_6),
    .Sum4(a_4bit_ripple_carry_adder_2_sum4), .Sum3(a_4bit_ripple_carry_adder_2_sum3),
    .Sum2(a_4bit_ripple_carry_adder_2_sum2), .Sum1(a_4bit_ripple_carry_adder_2_sum1), .Sum0(Z2));
  A_4bit_Ripple_Carry_Adder a_4bit_ripple_carry_adder_3 (
    .X3(a_4x1_multiplier_3_out_9), .Y2(a_4x1_multiplier_4_out_9), .X2(a_4x1_multiplier_3_out_8),
    .Y1(a_4x1_multiplier_4_out_8), .X1(a_4x1_multiplier_3_out_7), .Y0(a_4x1_multiplier_4_out_7),
    .X0(a_4x1_multiplier_3_out_6), .Sum4(a_4bit_ripple_carry_adder_3_sum4),
    .Sum3(a_4bit_ripple_carry_adder_3_sum3), .Sum2(a_4bit_ripple_carry_adder_3_sum2),
    .Sum1(a_4bit_ripple_carry_adder_3_sum1), .Sum0(Z1));  // open: Y3
  A_4x1_Multiplier a_4x1_multiplier_4 (
    .Y3(Y3), .Y2(Y2), .Y1(Y1), .Y0(Y0), .X(X0), .out_6(Z0), .out_7(a_4x1_multiplier_4_out_7),
    .out_8(a_4x1_multiplier_4_out_8), .out_9(a_4x1_multiplier_4_out_9));

  // Notes on the sheet:
  //   factor (4 bits)
  //   See the problem for details on this hint:   Build a 4x1-bit multiplier first!
  //   second factor (4 bits)
  //   product (8 bits)
  //   4-bit MULTIPLIER circuit
  //   most significant (highest) output bit
  //   least significant (lowest) output bit
endmodule

module A_3by2_divider (
  input  Y2,
  input  Y1,
  input  Y0,
  input  X1,
  input  X0,
  output Z2,
  output Z1,
  output Z0,
  output Error
);

  wire and_1_out, and_2_out, and_3_out, and_4_out, and_5_out, and_6_out, and_7_out, and_8_out, and_9_out,
       and_10_out, and_11_out, and_12_out, divide_by_one_1_first_digit, divide_by_one_1_last_digit,
       divide_by_one_1_out_5, divide_by_three_1_out_5, divide_by_three_1_out_6, divide_by_three_1_out_7,
       divide_by_two_1_first_digit, divide_by_two_1_last_digit, divide_by_two_1_out_5, not_1_out, not_2_out,
       not_3_out, not_4_out;

  Divide_By_One divide_by_one_1 (
    .in_1(Y2), .Y1(Y1), .in_3(Y0), .First_Digit(divide_by_one_1_first_digit), .out_5(divide_by_one_1_out_5),
    .Last_Digit(divide_by_one_1_last_digit));
  Divide_By_Two divide_by_two_1 (
    .Y1(Y2), .Y0(Y1), .FIRST_DIGIT(divide_by_two_1_first_digit), .out_5(divide_by_two_1_out_5),
    .LAST_DIGIT(divide_by_two_1_last_digit));  // open: HARDCODED_0
  Divide_By_Three divide_by_three_1 (
    .Y2(Y2), .Y1(Y1), .Y0(Y0), .in_4(Y0), .out_5(divide_by_three_1_out_5), .out_6(divide_by_three_1_out_6),
    .out_7(divide_by_three_1_out_7));
  and and_1 (and_1_out, divide_by_one_1_last_digit, and_4_out);
  and and_2 (and_2_out, divide_by_three_1_out_7, and_10_out);
  and and_3 (and_3_out, divide_by_one_1_first_digit, and_4_out);
  and and_4 (and_4_out, not_1_out, X0);
  and and_5 (and_5_out, divide_by_one_1_out_5, and_4_out);
  and and_6 (and_6_out, divide_by_two_1_first_digit, and_7_out);
  and and_7 (and_7_out, not_2_out, X1);
  and and_8 (and_8_out, divide_by_two_1_out_5, and_7_out);
  and and_9 (and_9_out, divide_by_two_1_last_digit, and_7_out);
  and and_10 (and_10_out, X0, X1);
  and and_11 (and_11_out, divide_by_three_1_out_5, and_10_out);
  and and_12 (and_12_out, divide_by_three_1_out_6, and_10_out);
  not not_1 (not_1_out, X1);
  not not_2 (not_2_out, X0);
  and and_13 (Error, not_3_out, not_4_out);
  not not_3 (not_3_out, X1);
  not not_4 (not_4_out, X0);
  or or_1 (Z2, and_3_out, and_6_out, and_11_out);
  or or_2 (Z1, and_5_out, and_8_out, and_12_out);
  or or_3 (Z0, and_1_out, and_9_out, and_2_out);

  // Notes on the sheet:
  //   Dividend (3 bits: Y2 Y1 Y0)
  //   Divisor (2 bits: X1 X0)
  //   Quotient (4 bits: Z2 Z1 Z0 and Error)
  //   3-by-2-bit DIVIDER circuit
endmodule

module A_2bit_decoder (
  input  I0,
  input  I1,
  output out_3,
  output out_4,
  output out_5,
  output out_6
);

  wire not_1_out, not_2_out, not_3_out, not_4_out;

  not not_1 (not_1_out, I0);
  not not_2 (not_2_out, I0);
  not not_3 (not_3_out, I1);
  not not_4 (not_4_out, I1);
  and and_1 (out_3, not_1_out, not_1_out, not_3_out);
  and and_2 (out_4, not_2_out, I1);
  and and_3 (out_5, I0, not_4_out);
  and and_4 (out_6, I0, I1);

  // Notes on the sheet:
  //   2-bit DECODER circuit (extra credit - see hw)
endmodule

module A_12nGb_memory (
  input  X2,
  input  X1,
  input  X0,
  input  A0,
  input  A1,
  input  READ,
  input  WRITE,
  output Q2,
  output Q1,
  output Q0
);

  wire a_2bit_decoder_1_out_3, a_2bit_decoder_1_out_4, a_2bit_decoder_1_out_5, a_2bit_decoder_1_out_6,
       and_1_out, and_2_out, and_3_out, and_4_out, and_5_out, and_6_out, and_7_out, and_8_out, and_9_out,
       and_10_out, and_11_out, and_12_out, and_13_out, and_14_out, and_15_out, and_16_out, and_17_out,
       and_18_out, and_19_out, and_20_out, flip_flop_1_q, flip_flop_2_q, flip_flop_3_q, flip_flop_4_q,
       flip_flop_5_q, flip_flop_6_q, flip_flop_7_q, flip_flop_8_q, flip_flop_9_q, flip_flop_10_q,
       flip_flop_11_q, flip_flop_12_q;

  and and_1 (and_1_out, a_2bit_decoder_1_out_3, READ);
  and and_2 (and_2_out, a_2bit_decoder_1_out_4, READ);
  and and_3 (and_3_out, a_2bit_decoder_1_out_5, READ);
  and and_4 (and_4_out, a_2bit_decoder_1_out_6, READ);
  A_2bit_decoder a_2bit_decoder_1 (
    .I0(A1), .I1(A0), .out_3(a_2bit_decoder_1_out_3), .out_4(a_2bit_decoder_1_out_4),
    .out_5(a_2bit_decoder_1_out_5), .out_6(a_2bit_decoder_1_out_6));
  and and_5 (and_5_out, a_2bit_decoder_1_out_3, WRITE);
  and and_6 (and_6_out, a_2bit_decoder_1_out_4, WRITE);
  and and_7 (and_7_out, a_2bit_decoder_1_out_5, WRITE);
  and and_8 (and_8_out, a_2bit_decoder_1_out_6, WRITE);
  Flip_flop flip_flop_1 (.DATA(X2), .STROBE(and_5_out), .Q(flip_flop_1_q));
  and and_9 (and_9_out, flip_flop_1_q, and_1_out);
  Flip_flop flip_flop_2 (.DATA(X2), .STROBE(and_6_out), .Q(flip_flop_2_q));
  and and_10 (and_10_out, and_2_out, flip_flop_2_q);
  Flip_flop flip_flop_3 (.DATA(X2), .STROBE(and_7_out), .Q(flip_flop_3_q));
  Flip_flop flip_flop_4 (.DATA(X2), .STROBE(and_8_out), .Q(flip_flop_4_q));
  and and_11 (and_11_out, and_4_out, flip_flop_4_q);
  and and_12 (and_12_out, flip_flop_3_q, and_3_out, and_10_out);
  or or_1 (Q2, and_11_out, and_12_out, and_10_out, and_9_out);
  Flip_flop flip_flop_5 (.DATA(X1), .STROBE(and_5_out), .Q(flip_flop_5_q));
  Flip_flop flip_flop_6 (.DATA(X1), .STROBE(and_6_out), .Q(flip_flop_6_q));
  and and_13 (and_13_out, flip_flop_6_q, and_2_out);
  Flip_flop flip_flop_7 (.DATA(X1), .STROBE(and_7_out), .Q(flip_flop_7_q));
  Flip_flop flip_flop_8 (.DATA(X1), .STROBE(and_8_out), .Q(flip_flop_8_q));
  and and_14 (and_14_out, flip_flop_8_q, and_4_out);
  and and_15 (and_15_out, flip_flop_5_q, and_1_out);
  and and_16 (and_16_out, flip_flop_7_q, and_3_out);
  or or_2 (Q1, and_14_out, and_13_out, and_16_out, and_15_out);
  Flip_flop flip_flop_9 (.DATA(X0), .STROBE(and_5_out), .Q(flip_flop_9_q));
  and and_17 (and_17_out, flip_flop_9_q, and_1_out);
  Flip_flop flip_flop_10 (.DATA(X0), .STROBE(and_6_out), .Q(flip_flop_10_q));
  and and_18 (and_18_out, flip_flop_10_q, and_2_out);
  Flip_flop flip_flop_11 (.DATA(X0), .STROBE(and_7_out), .Q(flip_flop_11_q));
  Flip_flop flip_flop_12 (.DATA(X0), .STROBE(and_8_out), .Q(flip_flop_12_q));
  and and_19 (and_19_out, flip_flop_12_q, and_4_out);
  and and_20 (and_20_out, flip_flop_11_q, and_3_out);
  or or_3 (Q0, and_19_out, and_20_out, and_18_out, and_17_out);

  // Notes on the sheet:
  //   12 nanogigabit MEMORY circuit (extra credit - see hw)
endmodule

module A_4x1_Multiplier (
  input  Y3,
  input  Y2,
  input  Y1,
  input  Y0,
  input  X,
  output out_6,
  output out_7,
  output out_8,
  output out_9
);

  and and_1 (out_9, Y3, X);
  and and_2 (out_8, Y2, X);
  and and_3 (out_7, Y1, X);
  and and_4 (out_6, Y0, X);
endmodule

module Divide_By_One (
  input  in_1,
  input  Y1,
  input  in_3,
  output First_Digit,
  output out_5,
  output Last_Digit
);


  assign First_Digit = in_1;
  assign Last_Digit = in_3;
  assign out_5 = Y1;

  // Notes on the sheet:
  //   Y2
  //   Y0
  //   First digit: For example in 10, 1 would be the first digit
endmodule

module Divide_By_Two (
  input  HARDCODED_0,
  input  Y1,
  input  Y0,
  output FIRST_DIGIT,
  output out_5,
  output LAST_DIGIT
);

  wire not_1_out;

  and and_1 (FIRST_DIGIT, HARDCODED_0, not_1_out);
  not not_1 (not_1_out, HARDCODED_0);

  assign LAST_DIGIT = Y0;
  assign out_5 = Y1;
endmodule

module Divide_By_Three (
  input  Y2,
  input  Y1,
  input  Y0,
  input  in_4,
  output out_5,
  output out_6,
  output out_7
);

  wire and_1_out, and_2_out, and_3_out, and_4_out, and_5_out, not_1_out, not_2_out, not_3_out, not_4_out,
       not_5_out, not_6_out;

  not not_1 (not_1_out, Y0);
  not not_2 (not_2_out, Y2);
  not not_3 (not_3_out, Y1);
  not not_4 (not_4_out, Y0);
  not not_5 (not_5_out, Y1);
  not not_6 (not_6_out, in_4);
  and and_1 (and_1_out, Y2, Y1, not_1_out);
  and and_2 (and_2_out, Y2, Y1, Y0);
  and and_3 (and_3_out, not_2_out, Y1, Y0);
  and and_4 (and_4_out, Y2, not_3_out, not_4_out);
  and and_5 (and_5_out, Y2, not_5_out, Y0);
  and and_6 (out_5, not_6_out, in_4);
  or or_1 (out_6, and_1_out, and_2_out);
  or or_2 (out_7, and_3_out, and_4_out, and_5_out);

  // Notes on the sheet:
  //   HARDCODED ZERO
  //   FIRST DIGIT
  //   LAST DIGIT
endmodule

module SR_Latch (
  input  STROBE,
  input  RESET,
  output Q
);

  wire not_1_out, not_2_out, not_3_out, not_4_out, or_1_out;

  not not_1 (not_1_out, STROBE);
  or or_1 (or_1_out, not_1_out, not_2_out);
  not not_2 (not_2_out, Q);
  not not_3 (not_3_out, or_1_out);
  or or_2 (Q, not_3_out, not_4_out);
  not not_4 (not_4_out, RESET);
endmodule

module Flip_flop (
  input  DATA,
  input  STROBE,
  output Q
);

  wire and_1_out, and_2_out, not_1_out;

  and and_1 (and_1_out, DATA, STROBE);
  not not_1 (not_1_out, DATA);
  and and_2 (and_2_out, not_1_out, STROBE);
  SR_Latch sr_latch_1 (.STROBE(and_1_out), .RESET(and_2_out), .Q(Q));
endmodule
